# Fritzing sketch LoRa Shield Sensors (saved by Fritzing 0.9.3b)

parts:
  Controller = Arduino Uno (Rev3)
  Temp = DS18B20 1-Wire Temperature Sensor [part_number=DS18B20]
  Temp/Feuchte = DHT22 Humidity and Temperature Sensor
  R2 = Resistor [tolerance=±5% resistance=4.7k package=THT]
  A/D-Wandler = HX711 Weighing Sensor Module
  Load_Cell1 = Load Cell - Red/white/black/green
  R1 = Resistor [tolerance=±5% resistance=4.7k package=THT]
  Temp1 = DS18B20 1-Wire Temperature Sensor [part_number=DS18B20]  # not connected
  ManualMode = Round Pushbutton
  LED1 = smd LED [color="Red (633nm)" package="0603 [SMD]"]
  R3 = Resistor [tolerance=±5% resistance=220 package=THT]

nets:
  N1: Controller.A0, A/D-Wandler.DO/RX
  N2: Controller.A1, A/D-Wandler.CK/TX
  N3: Controller.A2, LED1.cathode
  GND: Controller.GND, Temp.GND, Temp/Feuchte.GND, A/D-Wandler.GND, ManualMode.leg1
  N4: Controller.D3_PWM, ManualMode.leg0
  N5: Controller.D4, Temp/Feuchte.DATA, R1.Pin_1
  N6: Controller.D5_PWM, Temp.DQ, R2.Pin_1
  VDD: Controller.5V, Temp.VDD, Temp/Feuchte.VDD, R2.Pin_0, A/D-Wandler.VCC, R1.Pin_0, R3.Pin_0
  N7: A/D-Wandler.E+, Load_Cell1.wire4
  N8: A/D-Wandler.E-, Load_Cell1.wire1
  N9: A/D-Wandler.A+, Load_Cell1.wire3
  N10: A/D-Wandler.A-, Load_Cell1.wire2
  N11: LED1.anode, R3.Pin_1

custom parts:
  Load Cell - Red/white/black/green: A rectangle load cell/weighting pressure Sensor with four wires - Red, white, black, green. Normally corresponding with E+, E-, A+, A- respectively.
